# Fritzing sketch Layout3.3vMitSensor (saved by Fritzing 0.9.2b)
breadboards: 1

parts:
  Bauteil1 = Arduino Pro Mini v13
  J1 = shrouded pin header, 10 pins [form="♂ (shrouded male)"]
  R1 = Resistor [tolerance=±5% resistance=10k package=THT]
  DHT1 = DHT22 Humidity and Temperature Sensor

nets:
  N1: Bauteil1.D0/TX, J1.pin1
  VCC: Bauteil1.VCC, Bauteil1.RAW, J1.pin4, J1.pin5, DHT1.VDD
  GND: Bauteil1.GND, J1.pin2, DHT1.GND
  N2: Bauteil1.D4, R1.Pin_1, DHT1.DATA
  N3: J1.pin6, J1.pin7

// code stored in the sketch: KNXTest.ino
#include <Arduino.h>

#include <avr/sleep.h>
#include <KnxTpUart.h>
#include "DHT.h"

#define DHTPIN 4     
#define DHTTYPE DHT22 //DHT11, DHT21, DHT22

// Raum: Wohnzimmer, Address: 1.1.49, GroupTemperature: 0/7/1, GroupHumidity: 0/7/2
const String deviceAddress            = "1.1.49";
const String groupTemperatureAddress  = "0/7/1";
const String groupHumidityAddress     = "0/7/2";

const int interval = 60;
const int ledpin = 13;

DHT dht(DHTPIN, DHTTYPE);

KnxTpUart knx(&Serial, deviceAddress);

void setup()
{
  Serial.begin(19200);
  UCSR0C = UCSR0C | B00100000;  // Even Parity
  
  knx.uartReset();
  
  dht.begin();

  watchdogOn();                 // Watchdog timer einschalten.

  // The following saves some extra power by disabling some peripherals I am not using.
  ADCSRA = ADCSRA & B01111111;  // ADC abschalten, ADEN bit7 zu 0
  ACSR = B10000000;             // Analogen Comparator abschalten, ACD bit7 zu 1
  DIDR0 = DIDR0 | B00111111;    // Digitale Eingangspuffer ausschalten, analoge Eingangs Pins 0-5 auf 1
}

void loop()
{
  float temperature = dht.readTemperature();  //Temperatur auslesen
  knx.groupWrite2ByteFloat(groupTemperatureAddress, temperature);

  delay(5000);

  float humidity = dht.readHumidity();     //Luftfeuchte auslesen
  knx.groupWrite2ByteFloat(groupHumidityAddress, humidity);

  digitalWrite(ledpin, HIGH);
  delay(1000);
  digitalWrite(ledpin, LOW);

  pwrDown(interval - 1); // ATmega328 f�hrt runter f�r "interval" Sekunden;
}

void pwrDown(int seconds)
{
  set_sleep_mode(SLEEP_MODE_PWR_DOWN); // den tiefsten Schlaf ausw�hlen PWR_DOWN
  for(int i=0; i < seconds; i++)
  {
    sleep_enable();                    // sleep mode einschalten
    sleep_mode();                      // in den sleep mode gehen
    sleep_disable();                   // sleep mode ausschalten nach dem Erwachen
  }
}

void watchdogOn()
{
  MCUSR = MCUSR & B11110111;           // Reset flag ausschalten, WDRF bit3 vom MCUSR.
  WDTCSR = WDTCSR | B00011000;         // Bit 3+4 um danach den Prescaler setzen zu k�nnen
  WDTCSR = B00000110;                  // Watchdog Prescaler auf 128K setzen > ergibt ca. 1 Sekunde
  WDTCSR = WDTCSR | B01000000;         // Watchdog Interrupt einschalten
  MCUSR = MCUSR & B11110111;
}

ISR(WDT_vect)
{
  //sleepcounter ++; // Schlafzyklen mitz�hlen
}
